# Fritzing sketch Sketch(NANO) (saved by Fritzing 0.9.5d)
breadboards: 1

parts:
  Keypad4x4 = Keypad Membran 4x4
  Arduino_Nano(Rev3_0) = Arduino Nano (Rev3.0)
  LCD_display = LCD screen

nets:
  N1: Keypad4x4.Pin1, Arduino_Nano(Rev3_0).D2
  N2: Keypad4x4.Pin2, Arduino_Nano(Rev3_0).D3
  N3: Keypad4x4.Pin3, Arduino_Nano(Rev3_0).D4
  N4: Keypad4x4.Pin4, Arduino_Nano(Rev3_0).D5
  N5: Keypad4x4.Pin5, Arduino_Nano(Rev3_0).D6
  N6: Keypad4x4.Pin6, Arduino_Nano(Rev3_0).D7
  N7: Keypad4x4.Pin7, Arduino_Nano(Rev3_0).D8
  N8: Keypad4x4.Pin8, Arduino_Nano(Rev3_0).D9
  5V: Arduino_Nano(Rev3_0).5V, LCD_display.VDD
  N9: Arduino_Nano(Rev3_0).A5, LCD_display.DB5
  N10: Arduino_Nano(Rev3_0).A4, LCD_display.DB4
  GND: LCD_display.VSS

custom parts:
  Keypad Membran 4x4: Membrane Keypad 4x4 Matrix
