# Fritzing sketch Sketch(UNO) (saved by Fritzing 0.9.5d)
breadboards: 1

parts:
  S1 = Toggle Switch [package=THT]
  S2 = Toggle Switch [package=THT]
  S3 = Toggle Switch [package=THT]
  S4 = Toggle Switch [package=THT]
  S5 = Toggle Switch [package=THT]
  Servo_Motor = Basic Servo
  Arduino_UNO = Arduino Board Ethernet
  Power = Power plug
  K1 = KY-019 5V Relay Module [package="Breakout board"]
  K2 = KY-019 5V Relay Module [package="Breakout board"]
  K3 = KY-019 5V Relay Module [package="Breakout board"]
  WATER_PUMP1 = water pump/motor
  WATER_PUMP2 = water pump/motor
  WATER_PUMP3 = water pump/motor
  Servo_Motor_2 = Basic Servo

nets:
  N1: S1.COM, Arduino_UNO.D5_PWM
  GND: S1.L2, S2.L2, S3.L2, S4.L2, S5.L2, Power.GND, K1.-, K2.-, K3.-, WATER_PUMP1.pin_2, WATER_PUMP2.pin_2, WATER_PUMP3.pin_2, Servo_Motor_2.gnd
  N2: S2.COM, Arduino_UNO.D6_PWM
  N3: S3.COM, Arduino_UNO.D7
  N4: S4.COM, Arduino_UNO.D8
  N5: S5.COM, Arduino_UNO.D9_PWM
  GND_2: Servo_Motor.gnd, Arduino_UNO.GND
  VCC: Servo_Motor.vcc, Arduino_UNO.5V, K1.+, K2.+, K3.+
  N6: Servo_Motor.pulse, Arduino_UNO.D10_PWM/SS
  N7: Arduino_UNO.D11/MOSI, Servo_Motor_2.pulse
  N8: Arduino_UNO.D2_PWM, K1.S
  N9: Arduino_UNO.D3_PWM, K2.S
  N10: Arduino_UNO.D4, K3.S
  VCC_2: Power.VCC, K1.Common, K2.Common, K3.Common, Servo_Motor_2.vcc
  N11: K1.NO, WATER_PUMP3.pin_1
  N12: K2.NO, WATER_PUMP2.pin_1
  N13: K3.NO, WATER_PUMP1.pin_1

custom parts:
  KY-019 5V Relay Module: KY-019 5V Relay module, used to control AC circuits.
  water pump/motor: WATER PUMP BY ARDUBLOCKTR
